# Fritzing sketch Teil_1_Alexa steuert eine Lavalampe (saved by Fritzing 0.9.3b)
breadboards: 1

parts:
  JACK1 = 2.1mm Barrel Jack with Terminal Block
  M1 = RioRand LM2596
  U3 = 2-Channel 5v Relay Shield [package=relay-2ch5v10a]
  U7 = NodeMCU V3.0
  LED1 = LEDs [package=led10mm]

nets:
  N1: JACK1.POS, M1.Pin_2, U3.K1-In
  N2: JACK1.NEG, M1.Pin_1
  VCC: M1.Pin_3, U3.VCC, U7.Vin
  N3: M1.Pin_4, U3.GND, U7.GND#6, U7.GND#13, U7.GND#16, U7.GND#33
  N4: U3.IN1, U7.D0
  N5: U3.K1-On, LED1.C

custom parts:
  2-Channel 5v Relay Shield: 2 Channel 5v Relay Shield w. 2x SPD-06VDC-SD-C
  NodeMCU V3.0: ESP8266 based NodeMCU
  LEDs: LEDs Standard schematic elements and footprints for 5mm, 3mm, 1206, and 0603 sized LEDs. 5mm - Spark Fun Electronics SKU : COM-00529 (and others)
