# Fritzing sketch Teil_2_Alexa dimmt eine Schreibtischlampe (saved by Fritzing 0.9.4)
breadboards: 2

parts:
  JACK1 = 2.1mm Barrel Jack with Terminal Block
  M1 = RioRand LM2596
  LED1 = LEDs [package=led10mm]
  U1 = ESP32-38PinWide [part_number=ESP32-38PinWide]
  S1 = Pushbutton [package="[THT]"]
  Bauteil1 = IFR520 MOS module [package=THT]
  R1 = Resistor [tolerance=±5% resistance=15k package=THT]

nets:
  N1: JACK1.POS, M1.Pin_2, Bauteil1.GND, R1.Pin_0
  N2: JACK1.NEG, M1.Pin_1
  N3: M1.Pin_3, Bauteil1.VCC
  N4: M1.Pin_4, S1.Pin_3, S1.Pin_4
  N5: LED1.C, Bauteil1.V-
  N6: U1.GPIO16, Bauteil1.SIG, R1.Pin_1
  N7: U1.GPIO22, S1.Pin_1, S1.Pin_2

custom parts:
  LEDs: LEDs Standard schematic elements and footprints for 5mm, 3mm, 1206, and 0603 sized LEDs. 5mm - Spark Fun Electronics SKU : COM-00529 (and others)
  ESP32-38PinWide: Generic 38-Pin ESP32 with wide format (only access to one side of pins on a breadboard) based on Stephen Lilley's HiLetgo ESP-WROOM-32 ESP32 ESP-32S Development Board.
